# Fritzing sketch Blue Goji Breadboard (saved by Fritzing 0.9.3b)

parts:
  Part1 = Arduino Uno (Rev3)
  MD03A1 = Dual VNH2SP30 Motor Driver [part_number=MD03A]
  R1 = Rotary Potentiometer (Small) [maximum_resistance=100kΩ package=THT]
  M1 = DC Motor
  VCC1 = Battery block 9V
  R2 = Rotary Potentiometer (Small) [maximum_resistance=100kΩ package=THT]

nets:
  N1: Part1.A5/SCL, R2.wiper
  N2: Part1.D2, R1.wiper
  N3: Part1.D4, MD03A1.2INb#143
  N4: Part1.D5_PWM, MD03A1.2INb#142
  N5: Part1.D7, MD03A1.2CS
  N6: Part1.3V3, R1.leg1, R2.leg1
  GND: Part1.GND, MD03A1.GND, R1.leg2, VCC1.-, R2.leg2
  N7: MD03A1.OUT_2A, M1.pin_1
  N8: MD03A1.OUT_2B, M1.pin_2
  N9: MD03A1.VIN, VCC1.+

notes:
  Pedal Encoder
  Motor Pot
  Desired Resistance Input
  Steering Input
